# Fritzing sketch KredslÃ¸bsdiagram (saved by Fritzing 0.9.3b)
breadboards: 1

parts:
  U1 = 74HC595 SMD [package="SO16 [SMD]"]
  U2 = 7-SEGMENT-4DIGIT [package=7-segment-4digit-youngsun]
  R1 = Resistor [tolerance=±5% resistance=220 package="1206 [SMD]"]
  R2 = Resistor [tolerance=±5% resistance=220 package="1206 [SMD]"]
  R3 = Resistor [tolerance=±5% resistance=220 package="1206 [SMD]"]
  R4 = Resistor [tolerance=±5% resistance=220 package="1206 [SMD]"]
  R5 = Resistor [tolerance=±5% resistance=220 package="1206 [SMD]"]
  R6 = Resistor [tolerance=±5% resistance=220 package="1206 [SMD]"]
  R7 = Resistor [tolerance=±5% resistance=220 package="1206 [SMD]"]
  Part1 = Arduino Mega 2560 (Rev3)
  S1 = Pushbutton [package="[SMD]"]
  R9 = Resistor [tolerance=±5% resistance=220 package="1206 [SMD]"]
  C1 = Ceramic Capacitor [capacitance="100 nF" package="0603 [SMD, multilayer]"]

nets:
  N1: U1.Q1, U1.Q0, R1.Pin_0
  N2: U1.Q2, U2.8, R5.Pin_1
  N3: U1.Q3, R6.Pin_0
  N4: U1.Q4, R7.Pin_0
  N5: U1.Q5, R3.Pin_1
  N6: U1.Q6, R4.Pin_1
  N7: U1.MR, U1.VCC
  N8: U1.SH_CP, Part1.D22
  N9: U1.ST_CP, Part1.D24, C1.0
  N10: U1.OE, C1.1
  N11: U1.DS, Part1.D23
  N12: U2.1, R7.Pin_1
  N13: U2.2, R6.Pin_1
  N14: U2.4, R5.Pin_0
  N15: U2.5, R4.Pin_0
  N16: U2.7, Part1.D7_PWM
  N17: U2.9, R3.Pin_0
  N18: U2.11, Part1.D6_PWM
  N19: U2.13, Part1.D5_PWM
  N20: U2.14, R2.Pin_1
  N21: U2.15, R1.Pin_1
  N22: U2.16, Part1.D4_PWM
  N23: Part1.D3_PWM, S1.Pin_1, S1.Pin_2, R9.Pin_0
  N24: S1.Pin_3, S1.Pin_4

notes:
  lille kondensator
  Bemærk at displayet kun har 6 pins på hver side, så de 2 nederst længst til højre er der ikke
