# Fritzing sketch ADC_test (saved by Fritzing 0.9.3b)
breadboards: 1

parts:
  Part1 = Arduino Mega ADK (Rev3)
  U1 = PCM1803 [package=ssop20]
  R1 = Resistor [tolerance=±5% resistance=1k package="2010 [SMD]"]
  R2 = Resistor [tolerance=±5% resistance=1k package="2010 [SMD]"]
  R3 = Resistor [tolerance=±5% resistance=10k package="2010 [SMD]"]
  C1 = Capacitor [package=cap-pth-small2]

nets:
  N1: Part1.GND, U1.PDWN, U1.BPAS, U1.LRCK, R2.Pin_1
  N2: Part1.D10_PWM, U1.VCCA
  N3: Part1.D9_PWM, U1.VREF1
  N4: Part1.D8_PWM, U1.VINR
  N5: Part1.D7_PWM, U1.VINL
  N6: U1.VREF2, R3.Pin_1, C1.1
  N7: U1.TEST, R1.Pin_0, R2.Pin_0
  N8: U1.MD0, R3.Pin_0
  N9: U1.MD1, R1.Pin_1, C1.2

notes:
  PCM1803 = ADC0804
  Hvid ledning = analog signal ind

// code stored in the sketch: ADC_test_Kode.ino
/* Code written and tested by Christian Mark S164833
 * The code is written as a "setup guide"/help for using the ADC0804
 * "Analog-to-Digital Converter" with the Arduino. 
 * 
 * The hardware setup can be seen on the attached picture made in fritzing.
 * The rest of the pin-layout can be found one page 3 in this .pdf: http://www.ti.com/lit/ds/symlink/adc0802-n.pdf
 * See http://www.microcontroller-project.com/adc0804-pinout.html for a beginner friendly description of the the IC's pins
 */
#define CS 7 // Pin 1 på IC | Chip select (Active HIGH) - (This activates the chip)
#define RD 8 // Pin 2 på IC | Read (Active HIGHj) - (This will bring data from internal registers to the output pins after conversion)
#define WR 10 // PIN 3 på IC | Write (Active HIGH) - (Starts the conversion by taking in the analog value)
#define INTR 9 // Pin 5 på IC | Interupt request (Active HIGH) - (This pin automatically goes low when conversion is done by the IC)

void setup() {
  
  pinMode(WR, OUTPUT);
  digitalWrite(WR,HIGH);

  pinMode(INTR,INPUT);
  
  pinMode(RD,OUTPUT);
  
  pinMode(CS, OUTPUT);
  digitalWrite(CS,HIGH);
  
  Serial.begin(9600);

}

void loop() {      
      
      digitalWrite(CS,LOW); // Chip Select aktiv
      delay(10);
      digitalWrite(WR,LOW); // Starts the conversion by making the IC write the analog value to the internal registers   
      Serial.println("\nConversion start");
      digitalWrite(RD,LOW); // Read the values from the internal registers onto the output ports
      Serial.println("Conversion complete");
      delay(1000); // Wait 1 seconds to hold the value on the output ports (for visual representation only)
      digitalWrite(RD,HIGH); // Clear the output ports
      digitalWrite(WR,HIGH); // STOP conversion
      digitalWrite(CS,HIGH); // Chip Select deaktiveret

      delay(1000);

}

/* You should in theory make a check on the INTR ouput from the IC. But in reality the arduino functions "DigitalWrite()", "Serial.println()" and "digitalRead()"
 * are taking so much time, that the INTR signal is comming even before the arduino has a chance to read if the conversion is done. So i have included
 * some code that would read the input and a IF statement that would indicate that a "conversion is complete".
 
 int readD = 0; // Var to hold the INTR signal
 
 readD = digitalRead(INTR); // Read input INTR
 if(readD == HIGH){} // if INTR is HIGH, the IC tells us that the conversion is complete
     
 */
